# Fritzing sketch VL53LOX (saved by Fritzing 0.9.3b)

parts:
  Part1 = Adafruit VL53L0X Time of Flight Distance Sensor [part_number="Adafruit #3317"]
  Part2 = Adafruit VL53L0X Time of Flight Distance Sensor [part_number="Adafruit #3317"]
  Part4 = Arduino Uno (Rev3)
  Part5 = Adafruit VL53L0X Time of Flight Distance Sensor [part_number="Adafruit #3317"]

nets:
  VIN: Part1.VIN, Part2.VIN, Part4.5V, Part5.VIN
  GND: Part1.GND, Part2.GND, Part4.GND, Part5.GND
  N1: Part1.XSHUT, Part4.D6_PWM
  N2: Part1.SCL, Part2.SCL, Part4.A5/SCL, Part5.SCL
  N3: Part1.SDA, Part2.SDA, Part4.A4/SDA, Part5.SDA
  N4: Part2.XSHUT, Part4.D7
  N5: Part4.D5_PWM, Part5.XSHUT

custom parts:
  Adafruit VL53L0X Time of Flight Distance Sensor: The VL53L0X is a Time of Flight distance sensor like no other you've used! The sensor contains a very tiny invisible laser source, and a matching sensor. The VL53L0X can detect the "time of flight", or how long the light has taken to bounce back to the sensor. Since it uses a very narrow light source, it is good for determining distance of only the surface directly in front of it. Unlike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
